# Fritzing sketch fan_controller_uno (saved by Fritzing 0.9.9b)
breadboards: 1

parts:
  Part1 = Arduino Uno (Rev3)
  Q1 = Basic FET P-Channel [package="TO220 [THT]"]
  R1 = Resistor [tolerance=±5% power=0.25 resistance=10k package=THT]
  LED1 = LED - 5mm [color="Green (555nm)" current=0.030 package="5 mm [THT]"]
  R2 = Resistor [tolerance=±5% power=0.25 resistance=220 package=THT]
  D1 = Rectifier Diode [part_number=1N4001 package="300 mil [THT]"]
  L1 = Solenoid
  Part2 = DC Voltage Source 12V [package=THT]
  D2 = Rectifier Diode [part_number=1N4001 package="300 mil [THT]"]
  U1 = SWITCH_SPDT [package=kps-1290]
  U2 = SWITCH_SPDT [package=kps-1290]
  U3 = SWITCH_SPDT [package=kps-1290]
  U4 = SWITCH_SPDT [package=kps-1290]

nets:
  N1: Part1.D8, U3.S
  N2: Part1.D9_PWM, U4.O
  N3: Part1.D3_PWM, D2.anode
  N4: Part1.D4, Q1.gate, R1.Pin_1
  N5: Part1.D5_PWM, LED1.cathode
  N6: Part1.D6_PWM, U2.O
  N7: Part1.D7, U1.S
  N8: Part1.GND, Q1.source, R1.Pin_0, R2.Pin_0, U1.P, U2.P, U3.P, U4.P
  N9: Q1.drain, D1.anode, L1.pin1
  N10: LED1.anode, R2.Pin_1
  N11: D1.cathode, L1.pin2, Part2.V+

notes:
  PWM signal
  MODE Switch
  INTENSITY Switch
  Alternative MODE Switch (on-off only) via INT0
